# Fritzing sketch components (saved by Fritzing 0.9.2b)
breadboards: 1

parts:
  LP38798 = IC, DIP package, 12 pins [chip_label=LP38798]
  C_OUT = Electrolytic Capacitor [capacitance=10µF package="100 mil [THT, electrolytic]"]
  C_IN = Electrolytic Capacitor [capacitance=1µF package="100 mil [THT, electrolytic]"]
  C_CP = Ceramic Capacitor [capacitance=10nF package="100 mil [THT, multilayer]"]
  LM27761 = IC, DIP package, 8 pins [chip_label=LM27761]
  R1 = Resistor [tolerance=±5% resistance=59.8k package=THT]
  CIN = Electrolytic Capacitor [capacitance=4.7µF package="100 mil [THT, electrolytic]"]
  CCPOUT = Electrolytic Capacitor [capacitance=4.7µF package="100 mil [THT, electrolytic]"]
  C1 = Electrolytic Capacitor [capacitance=1µF package="100 mil [THT, electrolytic]"]
  COUT = Electrolytic Capacitor [capacitance=2.2µF package="100 mil [THT, electrolytic]"]
  R2 = Resistor [tolerance=±5% resistance=57k package=THT]
  R1_2 = Resistor [tolerance=±5% resistance=47.5k package=THT]
  R2_2 = Resistor [tolerance=±5% resistance=15k package=THT]
  LP5907-Q1 = IC, DIP package, 6 pins [chip_label=LP5907-Q1]
  C_OUT_2 = Electrolytic Capacitor [capacitance=1µF package="100 mil [THT, electrolytic]"]
  C_IN_2 = Electrolytic Capacitor [capacitance=1µF package="100 mil [THT, electrolytic]"]
  LP5907 = IC, DIP package, 4 pins [chip_label=LP5907]
  C_IN_3 = Electrolytic Capacitor [capacitance=1µF package="100 mil [THT, electrolytic]"]
  C_OUT_3 = Electrolytic Capacitor [capacitance=1µF package="100 mil [THT, electrolytic]"]

nets:
  5.50V V IN: LP38798.pin1, LP38798.pin2, LP38798.pin3, C_IN.+
  N1: LP38798.pin4, C_CP.1
  V EN: LP38798.pin5, LM27761.pin6
  DAP/GND: LP38798.pin6, LP38798.pin7, C_OUT.-, C_IN.-, C_CP.0, R2_2.Pin_1, LP5907-Q1.pin2, C_OUT_2.-, C_IN_2.-, LP5907.pin2, C_IN_3.-, C_OUT_3.-
  N2: LP38798.pin8, R1_2.Pin_0, R2_2.Pin_0
  N3: LP38798.pin9, R1_2.Pin_1
  V OUT 5.00V: LP38798.pin10, LP38798.pin11, LP38798.pin12, C_OUT.+
  To Supply: LM27761.pin1, CIN.+
  To GND Plane: LM27761.pin2, CIN.-, CCPOUT.-
  N4: LM27761.pin3, CCPOUT.+
  To Load: LM27761.pin4, R1.Pin_1, COUT.+
  N5: LM27761.pin5, R1.Pin_0, R2.Pin_0
  N6: LM27761.pin7, C1.-
  N7: LM27761.pin8, C1.+
  Thermal Pad: COUT.-, R2.Pin_1
  INPUT: LP5907-Q1.pin1, C_OUT_2.+, LP5907.pin1, C_OUT_3.+
  ENABLE: LP5907-Q1.pin3, LP5907.pin3
  OUTPUT: LP5907-Q1.pin6, C_IN_2.+, LP5907.pin4, C_IN_3.+
