# Fritzing sketch AD7779 & NodeMCU & nRF52832 (saved by Fritzing 0.9.2b)
breadboards: 1

parts:
  C1 = Ceramic Capacitor [capacitance=100nF package="100 mil [THT, multilayer]"]
  C2 = Ceramic Capacitor [capacitance=100nF package="100 mil [THT, multilayer]"]
  8_192MHz = Crystal [frequency="8 MHz" package=THT]
  C3 = Electrolytic Capacitor [capacitance=1µF package="100 mil [THT, electrolytic]"]
  C4 = Electrolytic Capacitor [capacitance=1µF package="100 mil [THT, electrolytic]"]
  C5 = Electrolytic Capacitor [capacitance=1µF package="100 mil [THT, electrolytic]"]
  C6 = Electrolytic Capacitor [capacitance=1µF package="100 mil [THT, electrolytic]"]
  C7 = Electrolytic Capacitor [capacitance=1µF package="100 mil [THT, electrolytic]"]
  C8 = Electrolytic Capacitor [capacitance=1µF package="100 mil [THT, electrolytic]"]
  C9 = Electrolytic Capacitor [capacitance=1µF package="100 mil [THT, electrolytic]"]
  C10 = Electrolytic Capacitor [capacitance=1µF package="100 mil [THT, electrolytic]"]
  C13 = Ceramic Capacitor [capacitance=100nF package="100 mil [THT, multilayer]"]
  U1 = NodeMCU V1.0
  Часть1 = AD7768 [chip_label=AD7779 package=QFN-64]
  C14 = Ceramic Capacitor [capacitance=100nF package="100 mil [THT, multilayer]"]
  C15 = Ceramic Capacitor [capacitance=100nF package="100 mil [THT, multilayer]"]
  C16 = Ceramic Capacitor [capacitance=100nF package="100 mil [THT, multilayer]"]
  C17 = Ceramic Capacitor [capacitance=100nF package="100 mil [THT, multilayer]"]
  C18 = Ceramic Capacitor [capacitance=100nF package="100 mil [THT, multilayer]"]
  C19 = Ceramic Capacitor [capacitance=100nF package="100 mil [THT, multilayer]"]
  C20 = Ceramic Capacitor [capacitance=100nF package="100 mil [THT, multilayer]"]
  C21 = Ceramic Capacitor [capacitance=100nF package="100 mil [THT, multilayer]"]
  C22 = Ceramic Capacitor [capacitance=100nF package="100 mil [THT, multilayer]"]
  C23 = Electrolytic Capacitor [capacitance=1µF package="100 mil [THT, electrolytic]"]
  Часть2 = CC2650 [chip_label=nRF52832 package=LQFP-48]
  32MHz_8pF_+-10ppm = Crystal [frequency="32 MHz" package=THT]
  32_768kHz_9pF_+-20ppm = Crystal [frequency="32 kHz" package=THT]
  U2 = usb to ttl [chip_label="usb to ttl" package="SIP (Single Inline) [THT]"]
  C24 = Ceramic Capacitor [capacitance=100nF package="100 mil [THT, multilayer]"]
  C25 = Ceramic Capacitor [capacitance=12pF package="100 mil [THT, multilayer]"]
  C26 = Ceramic Capacitor [capacitance=12pF package="100 mil [THT, multilayer]"]
  C27 = Ceramic Capacitor [capacitance=100nF package="100 mil [THT, multilayer]"]
  L1 = Inductor [inductance=3.9nH package="0603 [SMD]"]
  C28 = Ceramic Capacitor [capacitance=08pF package="100 mil [THT, multilayer]"]
  C30 = Electrolytic Capacitor [capacitance=1µF package="100 mil [THT, electrolytic]"]
  C31 = Electrolytic Capacitor [capacitance=4.7µF package="100 mil [THT, electrolytic]"]
  C32 = Ceramic Capacitor [capacitance=100nF package="100 mil [THT, multilayer]"]
  C33 = Ceramic Capacitor [capacitance=100nF package="100 mil [THT, multilayer]"]
  C34 = Ceramic Capacitor [capacitance=12pF package="100 mil [THT, multilayer]"]
  C35 = Ceramic Capacitor [capacitance=12pF package="100 mil [THT, multilayer]"]

nets:
  GND: C1.0, C2.0, C3.-, C4.-, C5.-, C6.-, C7.-, C8.-, C9.-, C10.-, C13.0, U1.GND, Часть1.AVSS1A, Часть1.REF1=, Часть1.DGND, Часть1.START, Часть1.REF2=, Часть1.AVSS1B, Часть1.AVSS2B, Часть1.AVSS3, Часть1.AVSS2A, Часть1.AVSS4, C14.0, C15.0, C16.0, C17.0, C18.0, C19.0, C20.0, C21.0, C22.0, C23.-, Часть2.VSS#30, Часть2.VSS#44, U2.gnd, C24.0, C25.0, C26.0, C27.0, C28.0, C30.-, C31.-, C32.1, C33.1, C34.1, C35.1
  3V3: C1.1, C2.1, C3.+, C4.+, C5.+, C6.+, C7.+, C10.+, C13.1, U1.3V3, Часть1.AVDD1A, Часть1.IOVDD, Часть1.AVDD1B, Часть1.AVDD2B, Часть1.FORMAT1, Часть1.FORMAT0, Часть1.CLK_SEL, Часть1.AVDD2A, Часть1.AVDD4, C15.1, C17.1, C19.1, Часть2.VDD, Часть2.VSS#47, U2.3v3, C24.1, C31.+, C32.0
  N1: 8_192MHz.pin_0, Часть1.XTAL1
  N2: 8_192MHz.pin_1, Часть1.XTAL2/MCLK
  N3: C8.+, Часть1.REF1+, C21.1
  N4: C9.+, Часть1.REF2+, C22.1
  N5: U1.D0, Часть1.RESET
  N6: U1.D1, Часть1.MODE3/ALERT
  N7: U1.D2, Часть1.DRDY, Часть2.P0.07
  N8: U1.D5, Часть1.DCLK2/SCLK
  N9: U1.D6, Часть1.DCLK0/SDO
  N10: U1.D7, Часть1.DCLK1/SDI
  N11: U1.D8, Часть1.ALERT/CS
  N12: U1.RX, Часть2.P0.27
  N13: U1.TX, Часть2.P0.26
  N14: Часть1.DREGCAP, C18.1, C23.+
  N15: Часть1.DOUT3, Часть2.P0.06
  N16: Часть1.DOUT2, Часть2.P0.05/AIN3
  N17: Часть1.DOUT1, Часть2.P0.04/AIN2
  N18: Часть1.DOUT0, Часть2.P0.03/AIN1
  N19: Часть1.DCLK, Часть2.P0.02/AIN0
  N20: Часть1.REF_OUT, C20.1
  N21: Часть1.AREG2CAP, C16.1
  N22: Часть1.AREG1CAP, C14.1
  N23: Часть2.DEC1, C33.0
  N24: Часть2.P0.00/XL1, 32_768kHz_9pF_+-20ppm.pin_0, C35.0
  N25: Часть2.P0.01/XL2, 32_768kHz_9pF_+-20ppm.pin_1, C34.0
  N26: Часть2.ANT, L1.pin_0, C28.1
  N27: Часть2.DEC3, C27.1
  N28: Часть2.XC1, 32MHz_8pF_+-10ppm.pin_1, C26.1
  N29: Часть2.XC2, 32MHz_8pF_+-10ppm.pin_0, C25.1
  N30: Часть2.DEC4, C30.+

custom parts:
  NodeMCU V1.0: ESP9266 based NodeMCU
  usb to ttl: A SIP stand-in part for whatever you want. With 5 pins on a 300 mil single inline package (SIP) footprint.

// code stored in the sketch: MAX11040K & NodeMCU.ino
/*
Pressure sensor system

This system shows how to log data from a analog sensor and log 
data into an SD card using the SD library.Also use an external 
24 bits ADC
   
created  20 June 2013
by Danny   
*/

#include <SPI.h>
//#include <SD.h>
//#include <LiquidCrystal.h>
#include <Wire.h>
#include "rgb_lcd.h"


const int ALERT_PIN=5;//D1
const int RESET_PIN=16;//D0
const int DRDY_PIN=4;//D2


const int GENERAL_USER_CONFIG_1_REG = 0x011;
const int GENERAL_USER_CONFIG_2_REG = 0x012;
const int GENERAL_USER_CONFIG_3_REG = 0x013;
const int DOUT_FORMAT_REG = 0x014;
const int ADC_MUX_CONFIG_REG = 0x015;

const int CH0_ERR_REG_REG = 0x04C;
const int CH1_ERR_REG_REG = 0x04D;
const int CH2_ERR_REG_REG = 0x04E;
const int CH3_ERR_REG_REG = 0x04F;
const int CH4_ERR_REG_REG = 0x050;
const int CH5_ERR_REG_REG = 0x051;
const int CH6_ERR_REG_REG = 0x052;
const int CH7_ERR_REG_REG = 0x053;
const int CH0_1_SAT_ERR_REG = 0x054;
const int CH2_3_SAT_ERR_REG = 0x055;
const int CH4_5_SAT_ERR_REG = 0x056;
const int CH6_7_SAT_ERR_REG = 0x057;
const int CHX_ERR_REG_EN_REG = 0x058;
const int GEN_ERR_REG_1_REG = 0x059;
const int GEN_ERR_REG_1_EN_REG = 0x05A;
const int GEN_ERR_REG_2_REG = 0x05B;
const int GEN_ERR_REG_2_EN_REG = 0x05C;
const int STATUS_REG_1_REG = 0x05D;
const int STATUS_REG_2_REG = 0x05E;
const int STATUS_REG_3_REG = 0x05F;


int alert;
int reset;
int drdy;


const int SDA_PIN=0;
const int CLK_PIN=2;

rgb_lcd lcd;
uint8_t char_cel[8] = {
  B00111, B00101, B00111, B00000, B00000, B00000, B00000
};


//const int SDCS = 4;
//const int ADCCS = 10;
const int ADCCS = 15;
double pressureValue0 = 0;
double pressureValue1 = 0;
double pressureValue2 = 0;
double pressureValue3 = 0;
//const int fs=3;
const int fs=250;
//LiquidCrystal lcd(12, 11, 6, 5, 3, 2);
//byte command11 = B01001000;//GENERAL_USER_CONFIG_1 0x011
//byte command11 = B01110100;//GENERAL_USER_CONFIG_1 0x011
byte command11 = B01110100;//GENERAL_USER_CONFIG_1 0x011
/*
7 ALL_CH_DIS_MCLK_EN If all ?-? channels are disabled, setting this bit high allows DCLK to
continue toggling.
 0x0 R/W
6 POWERMODE Power Mode.
 0x0 R/W
 0 Low power (1/4).
 1 High resolution.
5 PDB_VCM Power Down VCM Buffer. Active low. 
 0x1 R/W
4 PDB_REFOUT_BUF Power Down Internal Reference Output Buffer. Active low. 
 0x0 R/W
3 PDB_SAR Power Down SAR. Active low. 
 0x0 R/W
2 PDB_RC_OSC Power Down Signal for Internal Oscillator. Active low. 
 0x1 R/W
[1:0] SOFT_RESET Soft Reset
 0x0 R/W
 00 No effect
 01 No effect
 10 2nd write
 11 1st write
 */
byte command12 = B00011111;//GENERAL_USER_CONFIG_2 0x012
/*
[7:6] RESERVED Reserved. 
 0x0 R/W
5 SAR_DIAG_MODE_EN Sets SPI Interface to Read Back SAR Result on SDO. 
 0x0 R/W
[4:3] SDO_DRIVE_STR SDO Drive Strength. 
 0x1 R/W
 00 Nominal.
 01 Strong.
 10 Weak.
 11 Extra strong.
[2:1] DOUT_DRIVE_STR DOUTx Drive Strength.
 0x0 R/W
 00 Nominal.
 01 Strong.
 10 Weak.
 11 Extra strong.
0 SPI_SYNC SYNC Pulse Generated Through SPI.
 0x1 R/W
 0 This signal is AND?ed with the value on the START pin in the control module and generates a pulse in the SYNC_IN pin.
 1 This bit is AND?ed with the value on START pin in the control module.
 */
byte command13  = B11000000;//GENERAL_USER_CONFIG_3 0x013
byte command13_spi = B11010000;//GENERAL_USER_CONFIG_3 0x013
/*
[7:6] CONVST_DEGLITCH_DIS Disable deglitching of CONVST_SAR pin
 0x2 R/W
 00 Reserved.
 01 Reserved.
 10 CONVST_SAR Deglitch 1.5 MCLK.
 11 No deglitch circuit.
5 RESERVED Reserved. 
 0x0 R/W
4 SPI_SLAVE_MODE_EN Enable to SPI slave mode to read back ADC on SDO 
 0x0 R/W
[3:2] RESERVED Reserved. 
 0x0 R/W
1 RESERVED Reserved. 
 0x0 R/W
0 CLK_QUAL_DIS Disables the clock qualifier check if the user requires to use an MCLK
signal <265 kHz. 
 0x0 R/W
 */
byte command14 = B00000000;//DOUT_FORMAT 0x014
/*
[7:6] DOUT_FORMAT Data Out Format.
 0x0 R/W
 00 4 DOUT lines
 01 2 DOUT lines
 10 1 DOUT lines
 11 1 DOUT lines
5 DOUT_HEADER_FORMAT DOUT Header Format
 0x1 R/W
 0 Status header
 1 CRC header
4 RESERVED Reserved.
 0x0 R/W
[3:1] DCLK_CLK_DIV Divide MCLK
 0x0 R/W
0 RESERVED Reserved.
 0x0 R/W
 */
byte command15 = B01011000;//ADC_MUX_CONFIG 0x015
//byte command15 = B10011000;//ADC_MUX_CONFIG 0x015
/*
[7:6] REF_MUX_CTRL SD ADC Reference Mux
 0x0 R/W
 00 External reference REFx+/REFx?
 01 Internal reference.
 10 External supply AVDD1x/AVSSx.
 11 External reference REFx?/REFx+.
[5:2] MTR_MUX_CTRL SD ADC Meter Mux
 0x0 R/W
 0010 280 mV
 0011 External reference REFx+/REFx?
 0100 External reference REFx?/REFx+
 0101 External reference REFx?/REFx?
 0110 Internal reference +/?
 0111 Internal reference ?/+
 1000 Internal reference +/+
 1001 External reference REFx+/REFx+
[1:0] RESERVED Reserved.
 0x0 R/W
 */

//CH0_ERR_REG 0x04C
/*
[7:5] RESERVED Reserved 0x0 R/W
4 CH1_ERR_AINM_UV Channel 1?AIN1? Undervoltage Error 0x0 R
3 CH1_ERR_AINM_OV Channel 1?AIN1? Overvoltage Error 0x0 R
2 CH1_ERR_AINP_UV Channel 1?AIN1+ Undervoltage Error 0x0 R
1 CH1_ERR_AINP_OV Channel 1?AIN1+ Overvoltage Error 0x0 R
0 CH1_ERR_REF_DET Channel 1?Reference Detect Error 0x0 R
*/
//CH0_1_SAT_ERR 0x054
/*
5 CH1_ERR_MOD_SAT Channel 1?Modulator Output Saturation Error 0x0 R
4 CH1_ERR_FILTER_SAT Channel 1?Filter result has exceeded a reasonable level, before offset and
gain calibration has been applied 0x0 R
3 CH1_ERR_OUTPUT_SAT Channel 1?ADC conversion has exceeded limits and has been clamped 0x0 R
2 CH0_ERR_MOD_SAT Channel 0?Modulator Output Saturation Error 0x0 R
1 CH0_ERR_FILTER_SAT Channel 0?Filter result has exceeded a reasonable level, before offset and
gain calibration has been applied 0x0 R
0 CH0_ERR_OUTPUT_SAT Channel 0?ADC conversion has exceeded limits and has been clamped 0x0 R
*/

byte command58 = B11111111;//CHX_ERR_REG_EN 0x058
/*
7 OUTPUT_SAT_TEST_EN ADC Conversion Error Test Enable 0x1 R/W
6 FILTER_SAT_TEST_EN Filter Saturation Test Enable 0x1 R/W
5 MOD_SAT_TEST_EN Enable Error Flag for Modulator Saturation 0x1 R/W
4 AINM_UV_TEST_EN AINx? Undervoltage Test Enable 0x1 R/W
3 AINM_OV_TEST_EN AINx? Overvoltage Test Enable 0x1 R/W
2 AINP_UV_TEST_EN AINx+ Undervoltage Test Enable 0x1 R/W
1 AINP_OV_TEST_EN AINx+ Overvoltage Test Enable 0x1 R/W
0 REF_DET_TEST_EN Reference Detect Test Enable 0x0 R/W
*/

//GEN_ERR_REG_1 0x059
/*
5 MEMMAP_CRC_ERR A CRC of the memory map contents is run periodically to check for errors 0x0 R
4 ROM_CRC_ERR A CRC of the fuse contents is run periodically to check for errors in the fuses 0x0 R
3 SPI_CLK_COUNT_ERR SPI clock counter error 0x0 R
2 SPI_INVALID_READ_ERR SPI invalid read address 0x0 R
1 SPI_INVALID_WRITE_ERR SPI invalid write address 0x0 R
0 SPI_CRC_ERR SPI CRC error 0x0 R
*/
byte command5A = B11111110;//GEN_ERR_REG_1_EN 0x05A
//byte command5A = B11111111;//GEN_ERR_REG_1_EN 0x05A
/*
5 MEMMAP_CRC_TEST_EN Memory Map CRC Test Enable 0x1 R/W
4 ROM_CRC_TEST_EN Fuse CRC Test Enable 0x1 R/W
3 SPI_CLK_COUNT_TEST_EN SPI Clock Counter Test Enable 0x1 R/W
2 SPI_INVALID_READ_TEST_EN SPI Invalid Read Address Test Enable 0x1 R/W
1 SPI_INVALID_WRITE_TEST_EN SPI Invalid Write Address Test Enable 0x1 R/W
0 SPI_CRC_TEST_EN SPI CRC Error Test Enable 0x0 R/W
*/
//GEN_ERR_REG_2 0x05B
/*
5 RESET_DETECTED Reset Detected 0x0 R
4 EXT_MCLK_SWITCH_ERR Clock Not Switched Over 0x0 R
2 ALDO1_PSM_ERR AREG1CAP Power Supply Error 0x0 R
1 ALDO2_PSM_ERR AREG2CAP Power Supply Error 0x0 R
0 DLDO_PSM_ERR DREGCAP Power Supply Error 0x0 R
*/
//STATUS_REG_1 0x05D
/*
5 CHIP_ERROR Set this bit high if any error bit is high 0x0 R
4 ERR_LOC_CH4 An error specific to CH4_ERR_REG is active 0x0 R
3 ERR_LOC_CH3 An error specific to CH3_ERR_REG is active 0x0 R
2 ERR_LOC_CH2 An error specific to CH2_ERR_REG is active 0x0 R
1 ERR_LOC_CH1 An error specific to CH1_ERR_REG is active 0x0 R
0 ERR_LOC_CH0 An error specific to CH0_ERR_REG is active 0x0 R
*/
//STATUS_REG_2 0x05E
/*
5 CHIP_ERROR Set high if any error bit is high 0x0 R
4 ERR_LOC_GEN2 An error specific to GEN_ERR_REG_2 is active 0x0 R
3 ERR_LOC_GEN1 An error specific to GEN_ERR_REG_1 is active 0x0 R
2 ERR_LOC_CH7 An error specific to CH7_ERR_REG is active 0x0 R
1 ERR_LOC_CH6 An error specific to CH6_ERR_REG is active 0x0 R
0 ERR_LOC_CH5 An error specific to CH5_ERR_REG is active 0x0 R
*/
//STATUS_REG_3 0x05F
/*
5 CHIP_ERROR Set high if any error bit is high. 0x0 R
4 INIT_COMPLETE Fuse initialization is complete. Device is ready to receive commands. 0x0 R
3 ERR_LOC_SAT_CH6_7 An error specific to CH6_7_SAT_ERR register is active. 0x0 R
2 ERR_LOC_SAT_CH4_5 An error specific to CH4_5_SAT_ERR register is active. 0x0 R
1 ERR_LOC_SAT_CH2_3 An error specific to CH2_3_SAT_ERR register is active. 0x0 R
0 ERR_LOC_SAT_CH0_1 An error specific to CH0_1_SAT_ERR register is active. 0x0 R
*/


byte  CH0_ERR_REG;
byte  CH1_ERR_REG;
byte  CH2_ERR_REG;
byte  CH3_ERR_REG;
byte  CH4_ERR_REG;
byte  CH5_ERR_REG;
byte  CH6_ERR_REG;
byte  CH7_ERR_REG;
byte  CH0_1_SAT_ERR;
byte  CH2_3_SAT_ERR;
byte  CH4_5_SAT_ERR;
byte  CH6_7_SAT_ERR;
byte  GEN_ERR_REG_1;
byte  GEN_ERR_REG_2;
byte  STATUS_REG_1;
byte  STATUS_REG_2;
byte  STATUS_REG_3;

void setup()
{
//  lcd.setCursor(0, 0);
//  lcd.print("SOLDER STATION");
//  lcd.setCursor(0, 1);
//  lcd.print("ver. 0.5");

  pinMode(ALERT_PIN, INPUT);
  pinMode(RESET_PIN, OUTPUT);
  pinMode(DRDY_PIN, INPUT);

  pinMode(ADCCS, OUTPUT);
//  pinMode(SDCS, OUTPUT);
  digitalWrite(ADCCS, HIGH);
//  digitalWrite(SDCS, HIGH);
  SPI.begin();

  Wire.begin(SDA_PIN,CLK_PIN);
  lcd.begin(16, 2);
  lcd.createChar(1, char_cel);

  SPI.setBitOrder(MSBFIRST);

  digitalWrite(RESET_PIN, LOW);
    delayMicroseconds(10);
  digitalWrite(RESET_PIN, HIGH);
    delayMicroseconds(10);
  digitalWrite(RESET_PIN, LOW);
    delayMicroseconds(10);
  digitalWrite(RESET_PIN, HIGH);
    delayMicroseconds(10);
  digitalWrite(RESET_PIN, LOW);
    delayMicroseconds(10);
  digitalWrite(RESET_PIN, HIGH);
    delayMicroseconds(10);

    delayMicroseconds(10);
  digitalWrite(ADCCS, LOW);
  SPI.transfer(GENERAL_USER_CONFIG_1_REG);
  SPI.transfer(command11);
  digitalWrite(ADCCS, HIGH);
    delayMicroseconds(10);
  digitalWrite(ADCCS, LOW);
  SPI.transfer(GENERAL_USER_CONFIG_2_REG);
  SPI.transfer(command12);
  digitalWrite(ADCCS, HIGH);
    delayMicroseconds(10);
  digitalWrite(ADCCS, LOW);
  SPI.transfer(GENERAL_USER_CONFIG_3_REG);
  SPI.transfer(command13);
  digitalWrite(ADCCS, HIGH);
    delayMicroseconds(10);
  digitalWrite(ADCCS, LOW);
  SPI.transfer(DOUT_FORMAT_REG);
  SPI.transfer(command14);
  digitalWrite(ADCCS, HIGH);
    delayMicroseconds(10);
  digitalWrite(ADCCS, LOW);
  SPI.transfer(ADC_MUX_CONFIG_REG);
  SPI.transfer(command15);
  digitalWrite(ADCCS, HIGH);
    delayMicroseconds(10);
  digitalWrite(ADCCS, LOW);
  SPI.transfer(CHX_ERR_REG_EN_REG);
  SPI.transfer(command58);
  digitalWrite(ADCCS, HIGH);

    delayMicroseconds(10);

  digitalWrite(RESET_PIN, LOW);
    delayMicroseconds(10);
  digitalWrite(RESET_PIN, HIGH);
    delayMicroseconds(10);
  digitalWrite(RESET_PIN, LOW);
    delayMicroseconds(10);
  digitalWrite(RESET_PIN, HIGH);
    delayMicroseconds(10);
  digitalWrite(RESET_PIN, LOW);
    delayMicroseconds(10);
  digitalWrite(RESET_PIN, HIGH);
    delayMicroseconds(10);

    delayMicroseconds(10);
  digitalWrite(ADCCS, LOW);
  SPI.transfer(CH0_ERR_REG_REG);
  CH0_ERR_REG=SPI.transfer(0);
  digitalWrite(ADCCS, HIGH);
    delayMicroseconds(10);
  digitalWrite(ADCCS, LOW);
  SPI.transfer(CH1_ERR_REG_REG);
  CH1_ERR_REG=SPI.transfer(0);
  digitalWrite(ADCCS, HIGH);
    delayMicroseconds(10);
  digitalWrite(ADCCS, LOW);
  SPI.transfer(CH2_ERR_REG_REG);
  CH2_ERR_REG=SPI.transfer(0);
  digitalWrite(ADCCS, HIGH);
    delayMicroseconds(10);
  digitalWrite(ADCCS, LOW);
  SPI.transfer(CH3_ERR_REG_REG);
  CH3_ERR_REG=SPI.transfer(0);
  digitalWrite(ADCCS, HIGH);
    delayMicroseconds(10);
  digitalWrite(ADCCS, LOW);
  SPI.transfer(CH4_ERR_REG_REG);
  CH4_ERR_REG=SPI.transfer(0);
  digitalWrite(ADCCS, HIGH);
    delayMicroseconds(10);
  digitalWrite(ADCCS, LOW);
  SPI.transfer(CH5_ERR_REG_REG);
  CH5_ERR_REG=SPI.transfer(0);
  digitalWrite(ADCCS, HIGH);
    delayMicroseconds(10);
  digitalWrite(ADCCS, LOW);
  SPI.transfer(CH6_ERR_REG_REG);
  CH6_ERR_REG=SPI.transfer(0);
  digitalWrite(ADCCS, HIGH);
    delayMicroseconds(10);
  digitalWrite(ADCCS, LOW);
  SPI.transfer(CH7_ERR_REG_REG);
  CH7_ERR_REG=SPI.transfer(0);
  digitalWrite(ADCCS, HIGH);
    delayMicroseconds(10);
  digitalWrite(ADCCS, LOW);
  SPI.transfer(CH0_1_SAT_ERR_REG);
  CH0_1_SAT_ERR=SPI.transfer(0);
  digitalWrite(ADCCS, HIGH);
    delayMicroseconds(10);
  digitalWrite(ADCCS, LOW);
  SPI.transfer(CH2_3_SAT_ERR_REG);
  CH2_3_SAT_ERR=SPI.transfer(0);
  digitalWrite(ADCCS, HIGH);
    delayMicroseconds(10);
  digitalWrite(ADCCS, LOW);
  SPI.transfer(CH4_5_SAT_ERR_REG);
  CH4_5_SAT_ERR=SPI.transfer(0);
  digitalWrite(ADCCS, HIGH);
    delayMicroseconds(10);
  digitalWrite(ADCCS, LOW);
  SPI.transfer(CH6_7_SAT_ERR_REG);
  CH6_7_SAT_ERR=SPI.transfer(0);
  digitalWrite(ADCCS, HIGH);
    delayMicroseconds(10);
  digitalWrite(ADCCS, LOW);
  SPI.transfer(GEN_ERR_REG_1_REG);
  GEN_ERR_REG_1=SPI.transfer(0);
  digitalWrite(ADCCS, HIGH);
    delayMicroseconds(10);
  digitalWrite(ADCCS, LOW);
  SPI.transfer(GEN_ERR_REG_2_REG);
  GEN_ERR_REG_2=SPI.transfer(0);
  digitalWrite(ADCCS, HIGH);
    delayMicroseconds(10);
  digitalWrite(ADCCS, LOW);
  SPI.transfer(STATUS_REG_1_REG);
  STATUS_REG_1=SPI.transfer(0);
  digitalWrite(ADCCS, HIGH);
    delayMicroseconds(10);
  digitalWrite(ADCCS, LOW);
  SPI.transfer(STATUS_REG_2_REG);
  STATUS_REG_2=SPI.transfer(0);
  digitalWrite(ADCCS, HIGH);
    delayMicroseconds(10);
  digitalWrite(ADCCS, LOW);
  SPI.transfer(STATUS_REG_3_REG);
  STATUS_REG_3=SPI.transfer(0);
  digitalWrite(ADCCS, HIGH);


//  Serial.begin(9600);
  Serial.begin(115200);
  while (!Serial) {
    ; // wait for serial port to connect. Needed for Leonardo only
  }

    Serial.print(CH0_ERR_REG);
    Serial.print("; ");
    Serial.print(CH1_ERR_REG);
    Serial.print("; ");
    Serial.print(CH2_ERR_REG);
    Serial.print("; ");
    Serial.print(CH3_ERR_REG);
    Serial.print("; ");
    Serial.print(CH4_ERR_REG);
    Serial.print("; ");
    Serial.print(CH5_ERR_REG);
    Serial.print("; ");
    Serial.print(CH6_ERR_REG);
    Serial.print("; ");
    Serial.print(CH7_ERR_REG);
    Serial.print("; ");
    Serial.println("  ");    
    Serial.print(CH0_1_SAT_ERR);
    Serial.print("; ");
    Serial.print(CH2_3_SAT_ERR);
    Serial.print("; ");
    Serial.print(CH4_5_SAT_ERR);
    Serial.print("; ");
    Serial.print(CH6_7_SAT_ERR);
    Serial.print("; ");
    Serial.println("  ");    
    Serial.print(GEN_ERR_REG_1);
    Serial.print("; ");
    Serial.print(GEN_ERR_REG_2);
    Serial.print("; ");
    Serial.print(STATUS_REG_1);
    Serial.print("; ");
    Serial.print(STATUS_REG_2);
    Serial.print("; ");
    Serial.print(STATUS_REG_3);
    Serial.print("; ");
    Serial.println("  ");    

/*    lcd.setCursor(0, 0);
    lcd.print(GEN_ERR_REG_1);
    lcd.setCursor(8, 0);
    lcd.print(GEN_ERR_REG_2);
    lcd.setCursor(0, 1);
    lcd.print(STATUS_REG_1);
    lcd.setCursor(5, 1);
    lcd.print(STATUS_REG_2);
    lcd.setCursor(10, 1);
    lcd.print(STATUS_REG_3);*/

    delayMicroseconds(10);
  digitalWrite(ADCCS, LOW);
  SPI.transfer(GENERAL_USER_CONFIG_3_REG);
  SPI.transfer(command13_spi);
  digitalWrite(ADCCS, HIGH);
    delayMicroseconds(10);
    

/*  Serial.print("Initializing SD card...");
  if (!SD.begin(SDCS)) {
    Serial.println("Card failed, or not present");
    return;
  }
  Serial.println("card initialized.");*/
}

float volt0;
float volt1;
float volt2;
float volt3;
float volt4;
float volt5;
float volt6;
float volt7;
float v_ref=2.48;          // Reference Voltage, 5.0 Volt for LT1021 or 3.0 for LP2950-3
long int ltw0 = 0;         // ADC Data ling int
long int ltw1 = 0;
long int ltw2 = 0;
long int ltw3 = 0;  
long int ltw4 = 0;  
long int ltw5 = 0;  
long int ltw6 = 0;  
long int ltw7 = 0;  
long int cnt;                  // counter
byte b0;                  //
char st1[20];             // float voltage text
byte hdr0;                  
byte hdr1;                  
byte hdr2;                  
byte hdr3;                  
byte hdr4;                  
byte hdr5;                  
byte hdr6;                  
byte hdr7;                  

byte b00;
byte b01;
byte b02;
byte b03;
byte b04;
byte b05;
byte b06;
byte b07;
byte b08;
byte b09;
byte b10;
byte b11;
byte b12;
byte b13;
byte b14;
byte b15;
byte b16;
byte b17;
byte b18;
byte b19;
byte b20;
byte b21;
byte b22;
byte b23;
byte b24;
byte b25;
byte b26;
byte b27;
byte b28;
byte b29;
byte b30;
byte b31;

byte b32;
byte b33;
byte b34;
byte b35;
byte b36;
byte b37;
byte b38;
byte b39;
byte b40;
byte b41;
byte b42;
byte b43;
byte b44;
byte b45;
byte b46;
byte b47;

void loop()
{
/*
  digitalWrite(RESET_PIN, LOW);
    delayMicroseconds(1);
  digitalWrite(RESET_PIN, HIGH);
    delayMicroseconds(1);
  digitalWrite(RESET_PIN, LOW);
    delayMicroseconds(1);
  digitalWrite(RESET_PIN, HIGH);
    delayMicroseconds(1);
  digitalWrite(RESET_PIN, LOW);
*/
/*
    delayMicroseconds(1);
  digitalWrite(ADCCS, LOW);
  SPI.transfer(GENERAL_USER_CONFIG_1_REG);
  SPI.transfer(command11);
    delayMicroseconds(1);
  digitalWrite(ADCCS, HIGH);
    delayMicroseconds(1);
  digitalWrite(ADCCS, LOW);
  SPI.transfer(GENERAL_USER_CONFIG_2_REG);
  SPI.transfer(command12);
  digitalWrite(ADCCS, HIGH);
    delayMicroseconds(1);
  digitalWrite(ADCCS, LOW);
  SPI.transfer(GENERAL_USER_CONFIG_3_REG);
  SPI.transfer(command13);
    delayMicroseconds(1);
  digitalWrite(ADCCS, HIGH);
    delayMicroseconds(1);
  digitalWrite(ADCCS, LOW);
  SPI.transfer(ADC_MUX_CONFIG_REG);
  SPI.transfer(command15);
  digitalWrite(ADCCS, HIGH);
*/

/*    delayMicroseconds(10);
  digitalWrite(ADCCS, LOW);
  SPI.transfer(CH0_ERR_REG_REG);
  CH0_ERR_REG=SPI.transfer(0);
  digitalWrite(ADCCS, HIGH);
    delayMicroseconds(10);
  digitalWrite(ADCCS, LOW);
  SPI.transfer(CH1_ERR_REG_REG);
  CH1_ERR_REG=SPI.transfer(0);
  digitalWrite(ADCCS, HIGH);
    delayMicroseconds(10);
  digitalWrite(ADCCS, LOW);
  SPI.transfer(CH2_ERR_REG_REG);
  CH2_ERR_REG=SPI.transfer(0);
  digitalWrite(ADCCS, HIGH);
    delayMicroseconds(10);
  digitalWrite(ADCCS, LOW);
  SPI.transfer(CH3_ERR_REG_REG);
  CH3_ERR_REG=SPI.transfer(0);
  digitalWrite(ADCCS, HIGH);
    delayMicroseconds(10);
  digitalWrite(ADCCS, LOW);
  SPI.transfer(CH4_ERR_REG_REG);
  CH4_ERR_REG=SPI.transfer(0);
  digitalWrite(ADCCS, HIGH);
    delayMicroseconds(10);
  digitalWrite(ADCCS, LOW);
  SPI.transfer(CH5_ERR_REG_REG);
  CH5_ERR_REG=SPI.transfer(0);
  digitalWrite(ADCCS, HIGH);
    delayMicroseconds(10);
  digitalWrite(ADCCS, LOW);
  SPI.transfer(CH6_ERR_REG_REG);
  CH6_ERR_REG=SPI.transfer(0);
  digitalWrite(ADCCS, HIGH);
    delayMicroseconds(10);
  digitalWrite(ADCCS, LOW);
  SPI.transfer(CH7_ERR_REG_REG);
  CH7_ERR_REG=SPI.transfer(0);
  digitalWrite(ADCCS, HIGH);
    delayMicroseconds(10);
  digitalWrite(ADCCS, LOW);
  SPI.transfer(CH0_1_SAT_ERR_REG);
  CH0_1_SAT_ERR=SPI.transfer(0);
  digitalWrite(ADCCS, HIGH);
    delayMicroseconds(10);
  digitalWrite(ADCCS, LOW);
  SPI.transfer(CH2_3_SAT_ERR_REG);
  CH2_3_SAT_ERR=SPI.transfer(0);
  digitalWrite(ADCCS, HIGH);
    delayMicroseconds(10);
  digitalWrite(ADCCS, LOW);
  SPI.transfer(CH4_5_SAT_ERR_REG);
  CH4_5_SAT_ERR=SPI.transfer(0);
  digitalWrite(ADCCS, HIGH);
    delayMicroseconds(10);
  digitalWrite(ADCCS, LOW);
  SPI.transfer(CH6_7_SAT_ERR_REG);
  CH6_7_SAT_ERR=SPI.transfer(0);
  digitalWrite(ADCCS, HIGH);
    delayMicroseconds(10);
  digitalWrite(ADCCS, LOW);
  SPI.transfer(GEN_ERR_REG_1_REG);
  GEN_ERR_REG_1=SPI.transfer(0);
  digitalWrite(ADCCS, HIGH);
    delayMicroseconds(10);
  digitalWrite(ADCCS, LOW);
  SPI.transfer(GEN_ERR_REG_2_REG);
  GEN_ERR_REG_2=SPI.transfer(0);
  digitalWrite(ADCCS, HIGH);
    delayMicroseconds(10);
  digitalWrite(ADCCS, LOW);
  SPI.transfer(STATUS_REG_1_REG);
  STATUS_REG_1=SPI.transfer(0);
  digitalWrite(ADCCS, HIGH);
    delayMicroseconds(10);
  digitalWrite(ADCCS, LOW);
  SPI.transfer(STATUS_REG_2_REG);
  STATUS_REG_2=SPI.transfer(0);
  digitalWrite(ADCCS, HIGH);
    delayMicroseconds(10);
  digitalWrite(ADCCS, LOW);
  SPI.transfer(STATUS_REG_3_REG);
  STATUS_REG_3=SPI.transfer(0);
  digitalWrite(ADCCS, HIGH);*/

/*    Serial.print(CH0_ERR_REG,BIN);
    Serial.print(";");
    Serial.print(CH1_ERR_REG,BIN);
    Serial.print(";");
    Serial.print(CH2_ERR_REG,BIN);
    Serial.print(";");
    Serial.print(CH3_ERR_REG,BIN);
    Serial.print(";");
    Serial.print(CH4_ERR_REG,BIN);
    Serial.print(";");
    Serial.print(CH5_ERR_REG,BIN);
    Serial.print(";");
    Serial.print(CH6_ERR_REG,BIN);
    Serial.print(";");
    Serial.print(CH7_ERR_REG,BIN);
    Serial.print(";");
    Serial.println("");    
    Serial.print(CH0_1_SAT_ERR,BIN);
    Serial.print(";");
    Serial.print(CH2_3_SAT_ERR,BIN);
    Serial.print(";");
    Serial.print(CH4_5_SAT_ERR,BIN);
    Serial.print(";");
    Serial.print(CH6_7_SAT_ERR,BIN);
    Serial.print(";");
    Serial.println("");    
    Serial.print(GEN_ERR_REG_1,BIN);
    Serial.print(";");
    Serial.print(GEN_ERR_REG_2,BIN);
    Serial.print(";");
    Serial.print(STATUS_REG_1,BIN);
    Serial.print(";");
    Serial.print(STATUS_REG_2,BIN);
    Serial.print(";");
    Serial.print(STATUS_REG_3,BIN);
    Serial.print(";");
    Serial.println("");    
    Serial.println("");*/

/*    print_binary(CH0_ERR_REG,8);
    Serial.print(";");
    print_binary(CH1_ERR_REG,8);
    Serial.print(";");
    print_binary(CH2_ERR_REG,8);
    Serial.print(";");
    print_binary(CH3_ERR_REG,8);
    Serial.print(";");
    print_binary(CH4_ERR_REG,8);
    Serial.print(";");
    print_binary(CH5_ERR_REG,8);
    Serial.print(";");
    print_binary(CH6_ERR_REG,8);
    Serial.print(";");
    print_binary(CH7_ERR_REG,8);
    Serial.print(";");
    Serial.print(" ");    
    print_binary(CH0_1_SAT_ERR,8);
    Serial.print(";");
    print_binary(CH2_3_SAT_ERR,8);
    Serial.print(";");
    print_binary(CH4_5_SAT_ERR,8);
    Serial.print(";");
    print_binary(CH6_7_SAT_ERR,8);
    Serial.print(";");
    Serial.print(" ");    
    print_binary(GEN_ERR_REG_1,8);
    Serial.print(";");
    print_binary(GEN_ERR_REG_2,8);
    Serial.print(";");
    print_binary(STATUS_REG_1,8);
    Serial.print(";");
    print_binary(STATUS_REG_2,8);
    Serial.print(";");
    print_binary(STATUS_REG_3,8);
    Serial.print(";");
    Serial.println("");    
//    Serial.println("");    

    lcd.setCursor(0, 0);
    lcd.print(GEN_ERR_REG_1);
    lcd.setCursor(8, 0);
    lcd.print(GEN_ERR_REG_2);
    lcd.setCursor(0, 1);
    lcd.print(STATUS_REG_1);
    lcd.setCursor(5, 1);
    lcd.print(STATUS_REG_2);
    lcd.setCursor(10, 1);
    lcd.print(STATUS_REG_3);

    delay(1000/fs);

if(0)*/
{
/*
  lcd.print("0:");
  lcd.setCursor(9, 0);
  lcd.print("1:");
  lcd.setCursor(0, 1);
  lcd.print("2:");
  lcd.setCursor(9, 1);
  lcd.print("3:");
    */


  digitalWrite(ADCCS, LOW);
int drdy_pin=digitalRead(DRDY_PIN);
int miso=digitalRead(MISO);
  if (drdy_pin == LOW) {   // ADC Converter ready ?
  if (miso == LOW) {   // ADC Converter ready ?
    ltw0=0;
    ltw1=0;
    ltw2=0;
    ltw3=0;
    ltw4=0;
    ltw5=0;
    ltw6=0;
    ltw7=0;
//    SPI.transfer(B11110000);
    b0=SPI.transfer(0);
    b00=b0;
    hdr0 = b0;
    b0=SPI.transfer(0);
    b01=b0;
    ltw0 |= b0;
    ltw0 <<= 8;
    b0=SPI.transfer(0);
    b02=b0;
    ltw0 |= b0;
    ltw0 <<= 8;
    b0=SPI.transfer(0);
    b03=b0;
    ltw0 |= b0;   

    b0=SPI.transfer(0);
    b04=b0;
    hdr1 = b0;
    b0=SPI.transfer(0);
    b05=b0;
    ltw1 |= b0;
    ltw1 <<= 8;
    b0=SPI.transfer(0);
    b06=b0;
    ltw1 |= b0;
    ltw1 <<= 8;
    b0=SPI.transfer(0);
    b07=b0;
    ltw1 |= b0;   

    b0=SPI.transfer(0);
    b08=b0;
    hdr2 = b0;
    b0=SPI.transfer(0);
    b09=b0;
    ltw2 |= b0;
    ltw2 <<= 8;
    b0=SPI.transfer(0);
    b10=b0;
    ltw2 |= b0;
    ltw2 <<= 8;
    b0=SPI.transfer(0);
    b11=b0;
    ltw2 |= b0;   

    b0=SPI.transfer(0);
    b12=b0;
    hdr3 = b0;
    b0=SPI.transfer(0);
    b13=b0;
    ltw3 |= b0;
    ltw3 <<= 8;
    b0=SPI.transfer(0);
    b14=b0;
    ltw3 |= b0;
    ltw3 <<= 8;
    b0=SPI.transfer(0);
    b15=b0;
    ltw3 |= b0;   

    b0=SPI.transfer(0);
    b16=b0;
    hdr4 = b0;
    b0=SPI.transfer(0);
    b17=b0;
    ltw4 |= b0;
    ltw4 <<= 8;
    b0=SPI.transfer(0);
    b18=b0;
    ltw4 |= b0;
    ltw4 <<= 8;
    b0=SPI.transfer(0);
    b19=b0;
    ltw4 |= b0;   

    b0=SPI.transfer(0);
    b20=b0;
    hdr5 = b0;
    b0=SPI.transfer(0);
    b21=b0;
    ltw5 |= b0;
    ltw5 <<= 8;
    b0=SPI.transfer(0);
    b22=b0;
    ltw5 |= b0;
    ltw5 <<= 8;
    b0=SPI.transfer(0);
    b23=b0;
    ltw5 |= b0;   

    b0=SPI.transfer(0);
    b24=b0;
    hdr6 = b0;
    b0=SPI.transfer(0);
    b25=b0;
    ltw6 |= b0;
    ltw6 <<= 8;
    b0=SPI.transfer(0);
    b26=b0;
    ltw6 |= b0;
    ltw6 <<= 8;
    b0=SPI.transfer(0);
    b27=b0;
    ltw6 |= b0;   

    b0=SPI.transfer(0);
    b28=b0;
    hdr7 = b0;
    b0=SPI.transfer(0);
    b29=b0;
    ltw7 |= b0;
    ltw7 <<= 8;
    b0=SPI.transfer(0);
    b30=b0;
    ltw7 |= b0;
    ltw7 <<= 8;
    b0=SPI.transfer(0);
    b31=b0;
    ltw7 |= b0;   

    b0=SPI.transfer(0);    b32=b0;
    b0=SPI.transfer(0);    b33=b0;
    b0=SPI.transfer(0);    b34=b0;
    b0=SPI.transfer(0);    b35=b0;
    b0=SPI.transfer(0);    b36=b0;
    b0=SPI.transfer(0);    b37=b0;
    b0=SPI.transfer(0);    b38=b0;
    b0=SPI.transfer(0);    b39=b0;
    b0=SPI.transfer(0);    b40=b0;
    b0=SPI.transfer(0);    b41=b0;
    b0=SPI.transfer(0);    b42=b0;
    b0=SPI.transfer(0);    b43=b0;
    b0=SPI.transfer(0);    b44=b0;
    b0=SPI.transfer(0);    b45=b0;
    b0=SPI.transfer(0);    b46=b0;
    b0=SPI.transfer(0);    b47=b0;
    
    delayMicroseconds(1);

    digitalWrite(ADCCS, HIGH);      
    delayMicroseconds(1);

/*    Serial.print(b00);    Serial.print(";");
    Serial.print(b01);    Serial.print(";");
    Serial.print(b02);    Serial.print(";");
    Serial.print(b03);    Serial.print(";");
    Serial.print(b04);    Serial.print(";");
    Serial.print(b05);    Serial.print(";");
    Serial.print(b06);    Serial.print(";");
    Serial.print(b07);    Serial.print(";");
    Serial.print(b08);    Serial.print(";");
    Serial.print(b09);    Serial.print(";");
    Serial.print(b10);    Serial.print(";");
    Serial.print(b11);    Serial.print(";");
    Serial.print(b12);    Serial.print(";");
    Serial.print(b13);    Serial.print(";");
    Serial.print(b14);    Serial.print(";");
    Serial.print(b15);    Serial.print(";");
    Serial.print(b16);    Serial.print(";");
    Serial.print(b17);    Serial.print(";");
    Serial.print(b18);    Serial.print(";");
    Serial.print(b19);    Serial.print(";");
    Serial.print(b20);    Serial.print(";");
    Serial.print(b21);    Serial.print(";");
    Serial.print(b22);    Serial.print(";");
    Serial.print(b23);    Serial.print(";");
    Serial.print(b24);    Serial.print(";");
    Serial.print(b25);    Serial.print(";");
    Serial.print(b26);    Serial.print(";");
    Serial.print(b27);    Serial.print(";");
    Serial.print(b28);    Serial.print(";");
    Serial.print(b29);    Serial.print(";");
    Serial.print(b30);    Serial.print(";");
    Serial.print(b31);    Serial.print(";");
//    Serial.print(";  ");
    Serial.print(b32);    Serial.print(";");
    Serial.print(b33);    Serial.print(";");
    Serial.print(b34);    Serial.print(";");
    Serial.print(b35);    Serial.print(";");
    Serial.print(b36);    Serial.print(";");
    Serial.print(b37);    Serial.print(";");
    Serial.print(b38);    Serial.print(";");
    Serial.print(b39);    Serial.print(";");
    Serial.print(b40);    Serial.print(";");
    Serial.print(b41);    Serial.print(";");
    Serial.print(b42);    Serial.print(";");
    Serial.print(b43);    Serial.print(";");
    Serial.print(b44);    Serial.print(";");
    Serial.print(b45);    Serial.print(";");
    Serial.print(b46);    Serial.print(";");
    Serial.print(b47);    Serial.print(";");
    Serial.println(";  ");*/

/*    print_hex(b00,8);    Serial.print(";");
    print_hex(b01,8);    Serial.print(";");
    print_hex(b02,8);    Serial.print(";");
    print_hex(b03,8);    Serial.print(";");
    print_hex(b04,8);    Serial.print(";");
    print_hex(b05,8);    Serial.print(";");
    print_hex(b06,8);    Serial.print(";");
    print_hex(b07,8);    Serial.print(";");
    print_hex(b08,8);    Serial.print(";");
    print_hex(b09,8);    Serial.print(";");
    print_hex(b10,8);    Serial.print(";");
    print_hex(b11,8);    Serial.print(";");
    print_hex(b12,8);    Serial.print(";");
    print_hex(b13,8);    Serial.print(";");
    print_hex(b14,8);    Serial.print(";");
    print_hex(b15,8);    Serial.print(";");
    print_hex(b16,8);    Serial.print(";");
    print_hex(b17,8);    Serial.print(";");
    print_hex(b18,8);    Serial.print(";");
    print_hex(b19,8);    Serial.print(";");
    print_hex(b20,8);    Serial.print(";");
    print_hex(b21,8);    Serial.print(";");
    print_hex(b22,8);    Serial.print(";");
    print_hex(b23,8);    Serial.print(";");
    print_hex(b24,8);    Serial.print(";");
    print_hex(b25,8);    Serial.print(";");
    print_hex(b26,8);    Serial.print(";");
    print_hex(b27,8);    Serial.print(";");
    print_hex(b28,8);    Serial.print(";");
    print_hex(b29,8);    Serial.print(";");
    print_hex(b30,8);    Serial.print(";");
    print_hex(b31,8);    Serial.print(";");
//    Serial.print(";  ");
    print_hex(b32,8);    Serial.print(";");
    print_hex(b33,8);    Serial.print(";");
    print_hex(b34,8);    Serial.print(";");
    print_hex(b35,8);    Serial.print(";");
    print_hex(b36,8);    Serial.print(";");
    print_hex(b37,8);    Serial.print(";");
    print_hex(b38,8);    Serial.print(";");
    print_hex(b39,8);    Serial.print(";");
    print_hex(b40,8);    Serial.print(";");
    print_hex(b41,8);    Serial.print(";");
    print_hex(b42,8);    Serial.print(";");
    print_hex(b43,8);    Serial.print(";");
    print_hex(b44,8);    Serial.print(";");
    print_hex(b45,8);    Serial.print(";");
    print_hex(b46,8);    Serial.print(";");
    print_hex(b47,8);    Serial.print(";");
    Serial.println(";  ");*/

    print_binary(b00,8);    Serial.print(";");
    print_binary(b01,8);    Serial.print(";");
    print_binary(b02,8);    Serial.print(";");
    print_binary(b03,8);    Serial.print(";");
    print_binary(b04,8);    Serial.print(";");
    print_binary(b05,8);    Serial.print(";");
    print_binary(b06,8);    Serial.print(";");
    print_binary(b07,8);    Serial.print(";");
    print_hex(b08,8);    Serial.print(";");
    print_hex(b09,8);    Serial.print(";");
    print_hex(b10,8);    Serial.print(";");
    print_hex(b11,8);    Serial.print(";");
    print_hex(b12,8);    Serial.print(";");
    print_hex(b13,8);    Serial.print(";");
    print_hex(b14,8);    Serial.print(";");
    print_hex(b15,8);    Serial.print(";");
    print_hex(b16,8);    Serial.print(";");
    print_hex(b17,8);    Serial.print(";");
    print_hex(b18,8);    Serial.print(";");
    print_hex(b19,8);    Serial.print(";");
    print_hex(b20,8);    Serial.print(";");
    print_hex(b21,8);    Serial.print(";");
    print_hex(b22,8);    Serial.print(";");
    print_hex(b23,8);    Serial.print(";");
    print_hex(b24,8);    Serial.print(";");
    print_hex(b25,8);    Serial.print(";");
    print_hex(b26,8);    Serial.print(";");
    print_hex(b27,8);    Serial.print(";");
    print_hex(b28,8);    Serial.print(";");
    print_hex(b29,8);    Serial.print(";");
    print_hex(b30,8);    Serial.print(";");
    print_hex(b31,8);    Serial.print(";");
//    Serial.print(";  ");
    print_hex(b32,8);    Serial.print(";");
    print_hex(b33,8);    Serial.print(";");
    print_hex(b34,8);    Serial.print(";");
    print_hex(b35,8);    Serial.print(";");
    print_hex(b36,8);    Serial.print(";");
    print_hex(b37,8);    Serial.print(";");
    print_hex(b38,8);    Serial.print(";");
    print_hex(b39,8);    Serial.print(";");
    print_hex(b40,8);    Serial.print(";");
    print_hex(b41,8);    Serial.print(";");
    print_hex(b42,8);    Serial.print(";");
    print_hex(b43,8);    Serial.print(";");
    print_hex(b44,8);    Serial.print(";");
    print_hex(b45,8);    Serial.print(";");
    print_hex(b46,8);    Serial.print(";");
    print_hex(b47,8);    Serial.print(";");
    Serial.println(";  ");

    volt0 = ltw0 * v_ref*0.88*2/ 16777216; 
    volt1 = ltw1 * v_ref*0.88*2 / 16777216; 
    volt2 = ltw2 * v_ref*0.88*2 / 16777216; 
    volt3 = ltw3 * v_ref*0.88*2/ 16777216; 
    volt4 = ltw4 * v_ref*0.88*2/ 16777216; 
    volt5 = ltw5 * v_ref*0.88*2/ 16777216; 
    volt6 = ltw6 * v_ref*0.88*2/ 16777216; 
    volt7 = ltw7 * v_ref*0.88*2/ 16777216; 
    pressureValue0=(volt0-0.205)/0.01845;
    pressureValue1=(volt1-0.205)/0.01845;
    pressureValue2=(volt2-0.205)/0.01845;
    pressureValue3=(volt3-0.205)/0.01845;
//    Serial.println("ADC Converter ready");


  }
  }


  digitalWrite(ADCCS, HIGH);    
//  digitalWrite(SDCS, LOW);

/*  File dataFile = SD.open("datalog.txt", FILE_WRITE);
  // if the file is available, write to it:
  if (dataFile) {
    dataFile.println(pressureValue0);
    lcd.setCursor(2, 0);
    lcd.print(pressureValue0);
    lcd.setCursor(11, 0);
    lcd.print(pressureValue1);
    lcd.setCursor(2, 1);
    lcd.print(pressureValue2);
    lcd.setCursor(11, 1);
    lcd.print(pressureValue3);
  */  
/*    lcd.setCursor(0, 0);
    lcd.print(volt0,6);
    lcd.setCursor(8, 0);
    lcd.print(volt1,6);
    lcd.setCursor(0, 1);
    lcd.print(volt2,6);
    lcd.setCursor(8, 1);
    lcd.print(volt3,6);*/


/*    lcd.setCursor(0, 0);
    lcd.print(ltw0);
  ovrflw=digitalRead(OVRFLW_PIN);
  fault=digitalRead(FAULT_PIN);
    lcd.setCursor(0, 1);
    lcd.print(ovrflw);
    lcd.setCursor(8, 1);
    lcd.print(fault);*/
  
/*    // print to the serial port too:
    Serial.print(cnt++);
    Serial.print(";  ");*/

/*
 
   512  0000 0000 0000 0010 0000 0000
  1536  0000 0000 0000 0110 0000 0000
 34304  0000 0000 1000 0110 0000 0000
 38912  0000 0000 1001 1000 0000 0000
 42496  0000 0000 1010 0110 0000 0000
 44544  0000 0000 1010 1110 0000 0000
 46592  0000 0000 1011 0110 0000 0000
 
 */
    
/*    Serial.print(ltw0);           // print voltage as floating number
    Serial.print("; ");
    Serial.print(ltw1);
    Serial.print("; ");
    Serial.print(ltw2);
    Serial.print("; ");
    Serial.print(ltw3);
    Serial.print("; ");
    Serial.print(ltw4);
    Serial.print("; ");
    Serial.print(ltw5);
    Serial.print("; ");
    Serial.print(ltw6);
    Serial.print("; ");
    Serial.print(ltw7);
    Serial.print("; ");*/
    
/*    Serial.print(volt0,6);           // print voltage as floating number
    Serial.print("; ");
    Serial.print(volt1,6);
    Serial.print("; ");
    Serial.print(volt2,6);
    Serial.print("; ");
    Serial.print(volt3,6);
    Serial.print("; ");
    Serial.print(volt4,6);
    Serial.print("; ");
    Serial.print(volt5,6);
    Serial.print("; ");
    Serial.print(volt6,6);
    Serial.print("; ");
    Serial.print(volt7,6);
    Serial.print("; ");*/

/*
  Status Header Output
7 Alert
 This bit is set high if any of the enabled diagnostic functions have detected an error, including an
 external clock not detected, a memory map bit flip, or an internal CRC error. This bit is not channel specific.
 The bit clears if the error is no longer present.
6:4 CH_ID_[2:0]
 These bits indicate which ADC channel the following conversion data came from (see Table 32).
3 RESET_DETECTED
 This bit indicates if a reset condition occurs. This bit is not channel specific.
2 MODULATOR_SATURATE
 This bit indicates that the modulator output 20 consecutive 0s or 1s. The bit resets automatically after
 the error is no longer present.
1 FILTER_SATURATE
 This bit indicates that the filter output is out of bounds. The bit resets automatically after the error is
 no longer present.
0 AIN_OV_UVERROR
 This bit indicates that there is an AINx± overvoltage/undervoltage condition on the inputs. This bit is
 set until the appropriate register is read back and the error is no longer present.

8388608; 8388608; 8388608; 8388608; 8388608; 8388608; 8388608; 8388608; 
1000 0000 0000 0000 0000 0000

136 1000 1000
153 1001 1001
160 1010 0000
153 1001 1001
160 1010 0000
168 1010 1000
153 1001 1001
160 1010 0000

   2  0000 0010   2932
   6  0000 0110   7072
  15  0000 1111    183
 134  1000 0110  39363
 
 150  1001 0110
 152  1001 1000  85431
 154  1001 1010    177
 156  1001 1100      1
 158  1001 1110    174
 
 166  1010 0110   2357
 174  1010 1110  71976
 
 182  1011 0110    452


  67  0100 0011      3
  76  0100 1100     10
  87  0101 0111      8

   512  0000 0000 0000 0010 0000 0000
  1536  0000 0000 0000 0110 0000 0000
 34304  0000 0000 1000 0110 0000 0000
 38912  0000 0000 1001 1000 0000 0000
 42496  0000 0000 1010 0110 0000 0000
 44544  0000 0000 1010 1110 0000 0000
 46592  0000 0000 1011 0110 0000 0000

 */

    
/*    Serial.print(hdr0);
    Serial.print("; ");
    Serial.print(hdr1);
    Serial.print("; ");
    Serial.print(hdr2);
    Serial.print("; ");
    Serial.print(hdr3);
    Serial.print("; ");
    Serial.print(hdr4);
    Serial.print("; ");
    Serial.print(hdr5);
    Serial.print("; ");
    Serial.print(hdr6);
    Serial.print("; ");
    Serial.print(hdr7);
    Serial.print("; ");*/
    
/*    // print to the serial port too:
    Serial.print(cnt++);
    Serial.print(";  ");
    Serial.print(ltw0,6);           // print voltage as floating number
    Serial.print("; ");
    Serial.print(ltw1,6);
    Serial.print("; ");
    Serial.print(ltw2,6);
    Serial.print("; ");
    Serial.print(ltw3,6);
    Serial.print("; ");
    Serial.print(ltw4,6);
    Serial.print("; ");
    Serial.print(ltw5,6);
    Serial.print("; ");
    Serial.print(ltw6,6);
    Serial.print("; ");
    Serial.print(ltw7,6);
    Serial.print("; ");
  //  Serial.print(ltw0);
  //  Serial.print("; ");
    //Serial.print(pressureValue);  */

/*  alert=digitalRead(ALERT_PIN);
  drdy=digitalRead(DRDY_PIN);
    Serial.print(alert);
    Serial.print("; ");
    Serial.print(drdy);
    Serial.print("; ");
    Serial.print(drdy_pin);
    Serial.print("; ");
    Serial.print(miso);
    Serial.print("; ");
    Serial.println("  "); */   

//  lcd.setCursor(0, 0);
//    lcd.print(cnt);
//  lcd.setCursor(8, 0);
//    lcd.print(volt0,6);           // print voltage as floating number
//  lcd.setCursor(0, 1);
//    lcd.print(volt1,6);
//  lcd.setCursor(8, 1);
//    lcd.print(volt2,6);
//    lcd.print(volt3,6);
 

//    dataFile.close();
    delay(1000/fs);
//    lcd.clear();
/*  }  
  else {
    Serial.println("error opening datalog.txt");
  } */
//  digitalWrite(SDCS, HIGH);
} 
}

byte SPI_read()
{
  return SPI.transfer(0x00);
}




void print_binary(int v, int num_places)
{
    int mask=0, n;

    for (n=1; n<=num_places; n++)
    {
        mask = (mask << 1) | 0x0001;
    }
    v = v & mask;  // truncate v to specified number of places

    while(num_places)
    {

        if (v & (0x0001 << num_places-1))
        {
             Serial.print("1");
        }
        else
        {
             Serial.print("0");
        }

        --num_places;
        if(((num_places%4) == 0) && (num_places != 0))
        {
            Serial.print("_");
        }
    }
}

void print_hex(int v, int num_places)
{
    int mask=0, n, num_nibbles, digit;

    for (n=1; n<=num_places; n++)
    {
        mask = (mask << 1) | 0x0001;
    }
    v = v & mask; // truncate v to specified number of places

    num_nibbles = num_places / 4;
    if ((num_places % 4) != 0)
    {
        ++num_nibbles;
    }

    do
    {
        digit = ((v >> (num_nibbles-1) * 4)) & 0x0f;
        Serial.print(digit, HEX);
    } while(--num_nibbles);

}
